# Fritzing sketch chaotic_coaster-zero (saved by Fritzing 1.0.4)

parts:
  S1 = Taiway 100-SP-X-T1 SPDT Miniature Toggle Switch [part_number=100-SP-X-T1-0-0-B1-M2 package=THT]
  R3 = Photocell (LDR) [power=0.25W dark_resistance_@0.01lx=300kΩ light_resistance_@100lx=400Ω luminance=10lx package=THT]
  LED_Chain = ws2812b [package="smd 2812b"]  # not connected
  A2 = Waveshare rp2040-zero smd [package=SMD]
  R4 = Resistor [tolerance=±5% power=0.25W resistance=10k package=THT]
  DS2 = DS18B20 1-Wire Temperature Sensor Probe
  TP1 = TP4056 [chip_label=TP4056 package="DIP (Dual Inline) [THT]"]
  R2 = Resistor [tolerance=±5% power=0.25W resistance=10k package=THT]
  3_7v_Battery = LIPO-1000mAh [package=lipo-1000]
  S2 = Taiway 100-SP-X-T1 SPDT Miniature Toggle Switch [part_number=100-SP-X-T1-0-0-B1-M2 package=THT]
  TRS1 = Audio Jack (TRS) 3.5mm [package="4Ucon 08780 [THT]"]
  part = OLED 128x64 I2C Monochrome Display
  R1 = Resistor [tolerance=±5% power=0.25W resistance=4.7k package=THT]

nets:
  N1: S1.L1, A2.Pin_1, TP1.pin1
  N2: S1.L2, TP1.pin3
  N3: R3.pin_1, R2.Pin_0
  N4: A2.Pin_2, A2.Pin_33, DS2.GND, TP1.pin2, TP1.pin6, TRS1.Sleeve
  N5: A2.Pin_3, DS2.VDD, TRS1.Tip, R1.Pin_0
  N6: A2.Pin_10, DS2.DQ, TRS1.Ring, R1.Pin_1
  N7: A2.Pin_18, part.SCK
  N8: A2.Pin_19, part.SDA
  N9: R4.Pin_0, S2.L1
  N10: TP1.pin4, 3_7v_Battery.+
  N11: TP1.pin5, 3_7v_Battery.-

custom parts:
  Waveshare rp2040-zero smd: .RP2040-Zero, A Low-Cost, High-Performance Pico-Like MCU Board Based On Raspberry Pi Microcontroller RP2040. This varant is SMD with all the connections.
  TP4056: A DIP stand-in part for whatever IC you want. With 6 pins on a 300mil dual inline package (DIP) footprint.
